# Fritzing sketch bunnybot (saved by Fritzing 0.9.3b)

parts:
  WeMos_D1_Mini1 = WeMos D1 Mini
  J1 = Basic Servo
  J2 = Basic Servo
  J3 = Basic Servo

nets:
  5V: WeMos_D1_Mini1.5V, J2.vcc
  N1: WeMos_D1_Mini1.D5, J1.pulse
  N2: WeMos_D1_Mini1.D6, J2.pulse
  N3: WeMos_D1_Mini1.D7, J3.pulse
  N4: WeMos_D1_Mini1.G, J2.gnd
